# Fritzing sketch schema (saved by Fritzing 0.9.3b)
circuit board: 8.46667cm x 5.64444cm

parts:
  Composant1 = Arduino Nano (Rev3.0) (ICSP)
  U1 = DS1307 [package=so08]
  R2 = Slide Potentiometer [maximum_resistance=10kΩ]
  R3 = Slide Potentiometer [maximum_resistance=10kΩ]
  R4 = Slide Potentiometer [maximum_resistance=10kΩ]
  R5 = Resistor [tolerance=±5% resistance=440 package="2512 [SMD]"]
  R6 = Resistor [tolerance=±5% resistance=440 package="2512 [SMD]"]
  R7 = Resistor [tolerance=±5% resistance=440 package="2512 [SMD]"]
  R8 = Resistor [tolerance=±5% resistance=440 package="2512 [SMD]"]
  U2 = SWITCH_SPDT [package=kps-1290]
  U3 = SWITCH_SPDT [package=kps-1290]
  U4 = SWITCH_SPDT [package=kps-1290]
  R1 = Slide Potentiometer [maximum_resistance=10kΩ]
  JP1 = Header 6 [package=molex-1x6_lock]
  J1 = Basic Servo
  J2 = Basic Servo
  J3 = Power Jack [package=power_jack_pth_lock]
  J4 = Power Jack [package=power_jack_pth_lock]

nets:
  GND: Composant1.GND, U1.GND, R2.leg1, R3.leg1, R4.leg1, U2.S, U3.S, U4.S, R1.leg1, JP1.2, J1.gnd, J2.gnd, J3.GND, J4.GND
  N1: Composant1.D5, U2.P
  N2: Composant1.D6, U4.P
  N3: Composant1.D7, U3.P
  N4: Composant1.D9, JP1.4, J1.pulse
  N5: Composant1.D10, JP1.3, J2.pulse
  VCC: Composant1.5V, U1.VCC, R5.Pin_0, R6.Pin_0, R7.Pin_0, R8.Pin_0, JP1.1, J2.vcc, J4.PWR
  N6: Composant1.A5, U1.SCL
  N7: Composant1.A4, U1.SDA
  N8: Composant1.A3, R4.wiper
  N9: Composant1.A2, R3.wiper
  N10: Composant1.A1, R2.wiper
  N11: Composant1.A0, R1.wiper
  N12: R2.leg2, R5.Pin_1
  N13: R3.leg2, R7.Pin_1
  N14: R4.leg2, R8.Pin_1
  N15: R6.Pin_1, R1.leg2
  N16: J1.vcc, J3.PWR
